# Fritzing sketch Fingerprint_Scanner_Schematic (saved by Fritzing 0.9.3b)
breadboards: 1

parts:
  Part1 = Arduino Uno (Rev3) - ICSP
  R1 = Resistor [tolerance=±5% resistance=220 package="2512 [SMD]"]
  LED1 = smd LED [color="Red (633nm)" package="0603 [SMD]"]

nets:
  N1: Part1.D12/MISO, R1.Pin_0
  N2: Part1.GND, LED1.anode
  N3: R1.Pin_1, LED1.cathode
